# Fritzing sketch wifimote (saved by Fritzing 0.7.12b)
breadboards: 1

parts:
  D1 = Schottky Diode [part_number=1N5817 package="300 mil [THT]"]
  D2 = Schottky Diode [part_number=1N5817 package="300 mil [THT]"]
  D3 = Schottky Diode [part_number=1N5817 package="300 mil [THT]"]
  LM335_1 = LM35 Temperature Sensor [package="TO92 [THT]"]
  1K_R1 = Trimmer Potentiometer [maximum_resistance=1kΩ package=THT]
  Battery = Battery
  Solar = Battery
  3_3V_Reg = Voltage Regulator - 3.3V [package="TO220 [THT]"]
  C1_0_47uF = Ceramic Capacitor [package=THT]
  C2_470uF = Electrolytic Capacitor [package=THT]
  150R_R1 = 150 Ω Resistor [package=THT]
  LM335_2 = LM35 Temperature Sensor [package="TO92 [THT]"]
  1K_R2 = Trimmer Potentiometer [maximum_resistance=0.1MΩ package=THT]
  150R_R2 = 150 Ω Resistor [package=THT]
  WiFi = Generic female header - 10 pins [package=THT]
  WiFi_2 = Generic female header - 10 pins [package=THT]

nets:
  N1: D1.cathode, D2.anode, Battery.+
  N2: D1.anode, D3.anode, Solar.+
  N3: D2.cathode, D3.cathode, 3_3V_Reg.input_voltage, C1_0_47uF.pin_1
  N4: LM335_1.+Vs, 1K_R1.wiper
  N5: LM335_1.Vout, 150R_R1.Pin_0, WiFi_2.pin10
  GND: LM335_1.GND, 1K_R1.leg2, Battery.-, Solar.-, 3_3V_Reg.GND, C1_0_47uF.pin_0, C2_470uF.-, LM335_2.GND, 1K_R2.leg2, WiFi.pin10
  N6: 1K_R1.leg1, 3_3V_Reg.output_voltage, C2_470uF.+, 150R_R1.Pin_1, 1K_R2.leg1, 150R_R2.Pin_1, WiFi.pin1
  N7: LM335_2.+Vs, 1K_R2.wiper
  N8: LM335_2.Vout, 150R_R2.Pin_0, WiFi_2.pin9

notes:
  1
  +
  WiFiMote rev2 - http://ajf.io/wifimote
